// Logisim project Ctl_Data_Processing.circ as structural Verilog: 1 circuit, main circuit Data_Processing
module Data_Processing (
  input  Enable,
  input  [15:0] Instruction,
  output [2:0] Rd,
  output [2:0] Rn,
  output [2:0] Rm,
  output [3:0] ALU_Opcode,
  output [3:0] Flags_Update_Mask
);

  wire and_1_out;
  wire [2:0] Rm_t;
  wire [3:0] Flags_Update_Mask_t;

  Multiplexer #(.width(4)) multiplexer_1 (.out(Flags_Update_Mask_t));  // open: in0, in1, sel
  Multiplexer #(.width(3)) multiplexer_2 (.in0(Instruction[2:0]), .in1(Instruction[5:3]), .out(Rm_t), .sel(and_1_out));
  and and_1 (and_1_out, Instruction[6], ~Instruction[7], Instruction[8], Instruction[9]);  // AND_Gate
  // AND_Gate and_2 has open pins: in0=and_1_out, in1=Instruction[8], out=open
  Multiplexer #(.width(3)) multiplexer_3 (.in0(3'b000), .in1(Instruction[2:0]), .out(Rd), .sel(Enable));
  Multiplexer #(.width(3)) multiplexer_4 (.in0(3'b000), .in1(Rm_t), .out(Rn), .sel(Enable));
  Multiplexer #(.width(3)) multiplexer_5 (.in0(3'b000), .in1(Rm_t), .out(Rm), .sel(Enable));
  Multiplexer #(.width(4)) multiplexer_6 (.in0(4'b0000), .in1(Instruction[9:6]), .out(ALU_Opcode), .sel(Enable));
  Multiplexer #(.width(4)) multiplexer_7 (
    .in0(4'b0000), .in1(Flags_Update_Mask_t), .out(Flags_Update_Mask), .sel(Enable));

  // Other names for the same wires on the sheet: Rd_t[2:0] = Instruction[2:0]; ALU_Opcode_t[3:0] = Instruction[9:6];
  //   Rn_t[2:0] = Rm_t

  // Notes on the sheet:
  //   Note 2: RSB instruction has Rn as 1st operand.
  //   MUL instruction has Rn as 1st operand and Rdm as 2nd operand
  //   For simplification purposes, Rm is used for 1st operand both here and in the ALU.
  //   Note: instructions that does not save the result will still have the second operand as the destination register, the ALU will copy the second register to the destination register
  //   Pull output low on Enable = 0
endmodule
