// Logisim project Ctl_Load_Store.circ as structural Verilog: 1 circuit, main circuit Load_Store
module Load_Store (
  input  [15:0] Instruction,
  input  Enable,
  input  Clk,
  input  Reset,
  input  [31:0] Stack_Pointer,
  output Store,
  output Load,
  output PC_Hold,
  output [2:0] Rmd,
  output [31:0] RAM_Addr
);

  wire not_1_out, Store_Load;

  BitSelector #(.width(16)) bitselector_1 (.in(Instruction), .out(Store_Load), .sel(4'b0000));
  not not_1 (not_1_out, Store_Load);
  Multiplexer multiplexer_1 (.in0(1'b0), .in1(not_1_out), .out(Store), .sel(Enable));

  // Other names for the same wires on the sheet: CKL = Clk

  // Notes on the sheet:
  //   Instruction: pull=down
  //   Delay load and hold PC for 1 cycle for the RAM to send out requested data 
endmodule
